# Fritzing sketch Modulo Rele SRD 5V controlando motor a bateria de 12V (saved by Fritzing 0.9.2b)

parts:
  Parte1 = Arduino Uno (Rev3)
  KY-1 = Keyes Relay [package=THT]
  BAT1 = 12 battery [package=battery]
  M1 = DC Motor

nets:
  N1: Parte1.D10_PWM/SS, KY-1.signal
  N2: Parte1.5V, KY-1.power
  N3: Parte1.GND, KY-1.ground
  N4: KY-1.NC, BAT1.-
  N5: KY-1.C, M1.pin_2
  N6: BAT1.+, M1.pin_1

custom parts:
  Keyes Relay: The Keyes 5V relay module is suitable for SCM development, home appliance control. It uses a 5V~12V TIL control signal which can control DC / AC signal.
  12 battery: 12V lead acid type battery, like the Husqvarna YTH2448 12V 35AH battery. This is the mini version 1/4 the size of the actual battery to be closer to typical breadboard parts (around 2in wide rathher than 7in). The pads in pcb are sized to accomidate up to 14ga wire (as these batterys will deliver high currents.)
